# Fritzing sketch button_switched_diode (saved by Fritzing 0.8.3b)
breadboards: 1

parts:
  R1 = Resistor [tolerance=±5% resistance=470 package=THT]
  Part1 = Arduino Uno (Rev3)
  LED1 = LED - 5mm [color="Red (633nm)" package="5 mm [THT]"]  # not connected
  S1 = Pushbutton [package="[THT]"]

nets:
  N1: R1.Pin_1, Part1.GND, S1.Pin_3, S1.Pin_4
  N2: Part1.A0, S1.Pin_1, S1.Pin_2
